// Logisim project 16b_processor_bps16_wds9.circ as structural Verilog: 7 circuits, main circuit main
module main (
  input  in_1,
  output [1:0] Format
);

  wire clock_1_out, instDecoder_p2, registerfile_1_p3, registerfile_1_p4, registerfile_1_p6;
  wire [2:0] instDecoder_p5, registerfile_1_p5;
  wire [3:0] instDecoder_p7;
  wire [15:0] multiplexer_1_out, PC_q, registerfile_1_p1, registerfile_1_p7, registerfile_1_p8, rom_1_data;

  Counter #(.width(16), .max('hffff)) PC (
    .load(instDecoder_p2), .D(multiplexer_1_out), .count(1'b1), .Q(PC_q), .clk(clock_1_out), .clr(in_1));  // open: carry
  Clock clock_1 (.out(clock_1_out));
  Multiplexer #(.width(16), .enable("false")) multiplexer_1 (
    .in1(registerfile_1_p7), .out(multiplexer_1_out), .sel(instDecoder_p2));  // open: in0
  ROM #(.addrWidth(16), .dataWidth(16)) rom_1 (.addr(PC_q), .data(rom_1_data));  // open: sel
  // RegisterFile registerfile_1: pin names not known; wires that end beside it: registerfile_1_p1, clock_1_out, registerfile_1_p3, registerfile_1_p4, registerfile_1_p5, registerfile_1_p6, registerfile_1_p7, registerfile_1_p8
  Multiplexer #(.width(3), .enable("false")) multiplexer_2 (
    .in0(instDecoder_p5), .in1(3'b111), .out(registerfile_1_p5));  // open: sel
  // instrDecode instDecoder: pin names not known; wires that end beside it: rom_1_data, instDecoder_p2, registerfile_1_p4, registerfile_1_p3, instDecoder_p5, registerfile_1_p6, instDecoder_p7, Format
  alu ALU (
    .in1(registerfile_1_p7), .in2(registerfile_1_p8), .opCode(instDecoder_p7), .Result(registerfile_1_p1));  // open: shAmt
  RAM ram_1 (.clk(clock_1_out));  // open: addr, data, sel, ld, clr

  // Notes on the sheet:
  //   contents of rom_1 (hex, n*v repeats v):
  //   3708 1708 14*0 8
endmodule

module _16b_rAdder (
  input  [15:0] in1,
  input  [15:0] in2,
  output cOut,
  output [15:0] sum
);

  wire n1b_adder_1_cout, n1b_adder_2_cout, n1b_adder_3_cout, n1b_adder_4_cout, n1b_adder_5_cout,
       n1b_adder_6_cout, n1b_adder_7_cout, n1b_adder_8_cout, n1b_adder_9_cout, n1b_adder_10_cout,
       n1b_adder_11_cout, n1b_adder_12_cout, n1b_adder_13_cout, n1b_adder_14_cout, n1b_adder_15_cout;

  _1b_adder u_1b_adder_1 (.Input_1(in2[0]), .Input_2(in1[0]), .c_in(1'b0), .Sum(sum[0]), .Cout(n1b_adder_1_cout));
  _1b_adder u_1b_adder_2 (
    .Input_1(in2[1]), .Input_2(in1[1]), .c_in(n1b_adder_1_cout), .Sum(sum[1]), .Cout(n1b_adder_2_cout));
  _1b_adder u_1b_adder_3 (
    .Input_1(in2[2]), .Input_2(in1[2]), .c_in(n1b_adder_2_cout), .Sum(sum[2]), .Cout(n1b_adder_3_cout));
  _1b_adder u_1b_adder_4 (
    .Input_1(in2[3]), .Input_2(in1[3]), .c_in(n1b_adder_3_cout), .Sum(sum[3]), .Cout(n1b_adder_4_cout));
  _1b_adder u_1b_adder_5 (
    .Input_1(in2[4]), .Input_2(in1[4]), .c_in(n1b_adder_4_cout), .Sum(sum[4]), .Cout(n1b_adder_5_cout));
  _1b_adder u_1b_adder_6 (
    .Input_1(in2[5]), .Input_2(in1[5]), .c_in(n1b_adder_5_cout), .Sum(sum[5]), .Cout(n1b_adder_6_cout));
  _1b_adder u_1b_adder_7 (
    .Input_1(in2[6]), .Input_2(in1[6]), .c_in(n1b_adder_6_cout), .Sum(sum[6]), .Cout(n1b_adder_7_cout));
  _1b_adder u_1b_adder_8 (
    .Input_1(in2[7]), .Input_2(in1[7]), .c_in(n1b_adder_7_cout), .Sum(sum[7]), .Cout(n1b_adder_8_cout));
  _1b_adder u_1b_adder_9 (
    .Input_1(in2[8]), .Input_2(in1[8]), .c_in(n1b_adder_8_cout), .Sum(sum[8]), .Cout(n1b_adder_9_cout));
  _1b_adder u_1b_adder_10 (
    .Input_1(in2[9]), .Input_2(in1[9]), .c_in(n1b_adder_9_cout), .Sum(sum[9]), .Cout(n1b_adder_10_cout));
  _1b_adder u_1b_adder_11 (
    .Input_1(in2[10]), .Input_2(in1[10]), .c_in(n1b_adder_10_cout), .Sum(sum[10]), .Cout(n1b_adder_11_cout));
  _1b_adder u_1b_adder_12 (
    .Input_1(in2[11]), .Input_2(in1[11]), .c_in(n1b_adder_11_cout), .Sum(sum[11]), .Cout(n1b_adder_12_cout));
  _1b_adder u_1b_adder_13 (
    .Input_1(in2[12]), .Input_2(in1[12]), .c_in(n1b_adder_12_cout), .Sum(sum[12]), .Cout(n1b_adder_13_cout));
  _1b_adder u_1b_adder_14 (
    .Input_1(in2[13]), .Input_2(in1[13]), .c_in(n1b_adder_13_cout), .Sum(sum[13]), .Cout(n1b_adder_14_cout));
  _1b_adder u_1b_adder_15 (
    .Input_1(in2[14]), .Input_2(in1[14]), .c_in(n1b_adder_14_cout), .Sum(sum[14]), .Cout(n1b_adder_15_cout));
  _1b_adder u_1b_adder_16 (.Input_1(in2[15]), .Input_2(in1[15]), .c_in(n1b_adder_15_cout), .Sum(sum[15]), .Cout(cOut));
endmodule

module _1b_adder (
  input  Input_1,
  input  Input_2,
  input  c_in,
  output Sum,
  output Cout
);

  wire and_1_out, and_2_out, xor_1_out;

  xor xor_1 (xor_1_out, Input_1, Input_2);
  and and_1 (and_1_out, Input_1, Input_2);
  xor xor_2 (Sum, xor_1_out, c_in);
  and and_2 (and_2_out, xor_1_out, c_in);
  or or_1 (Cout, and_1_out, and_2_out);
endmodule

module alu (
  input  [15:0] in1,
  input  [15:0] in2,
  input  [2:0] shAmt,
  input  [3:0] opCode,
  output [15:0] Result
);

  wire [15:0] _16bAdder_sum, and_1_out, multiplexer_1_out, multiplexer_2_out, multiplexer_3_out,
       n16b_radder_1_sum, not_1_out, xor_1_out;

  assign not_1_out = ~in2;  // NOT_Gate not_1, 16 bits wide
  _16b_rAdder u_16b_radder_1 (.in1(not_1_out), .in2(16'h1), .sum(n16b_radder_1_sum));  // open: cOut
  Multiplexer #(.width(16), .enable("false")) multiplexer_1 (
    .in0(in2), .in1(n16b_radder_1_sum), .out(multiplexer_1_out), .sel(opCode[1]));
  assign and_1_out = in1 & in2;  // AND_Gate and_1, 16 bits wide
  assign xor_1_out = in1 ^ in2;  // XOR_Gate xor_1, 16 bits wide
  Multiplexer #(.width(16), .enable("false")) multiplexer_2 (
    .in0(and_1_out), .in1(xor_1_out), .out(multiplexer_2_out), .sel(opCode[0]));
  _16b_rAdder _16bAdder (.in1(in1), .in2(multiplexer_1_out), .sum(_16bAdder_sum));  // open: cOut
  Multiplexer #(.width(16), .enable("false")) multiplexer_3 (
    .in0(multiplexer_2_out), .out(multiplexer_3_out), .sel(opCode[1]));  // open: in1
  Multiplexer #(.width(16), .enable("false")) multiplexer_4 (
    .in0(_16bAdder_sum), .in1(multiplexer_3_out), .out(Result), .sel(opCode[2]));
endmodule

module instrDecode (
  input  [15:0] Instruction,
  output [2:0] rD,
  output [2:0] rS,
  output [2:0] rT,
  output [2:0] shAmt,
  output [3:0] opCode,
  output [5:0] Immediate,
  output [11:0] Address,
  output ret,
  output WE,
  output [1:0] iFormat
);

  wire not_1_out, or_1_out, xor_1_out;

  ret ret_1 (.opCode(Instruction[15:12]), .ret(ret));
  wEnable wenable_1 (.opCode(Instruction[15:12]), .WE(WE));
  xor xor_1 (xor_1_out, Instruction[13], Instruction[14]);
  or or_1 (or_1_out, Instruction[12], Instruction[14]);
  not not_1 (not_1_out, Instruction[15]);
  and and_1 (iFormat[0], or_1_out, not_1_out);
  and and_2 (iFormat[1], Instruction[12], Instruction[15], xor_1_out);

  assign Address = Instruction[11:0];
  assign Immediate = Instruction[5:0];
  assign opCode = Instruction[15:12];
  assign rD = Instruction[5:3];
  assign rS = Instruction[11:9];
  assign rT = Instruction[8:6];
  assign shAmt = Instruction[2:0];
endmodule

module wEnable (
  input  [3:0] opCode,
  output WE
);

  wire and_1_out, and_2_out, and_3_out, not_1_out, not_2_out, not_3_out, not_4_out;

  not not_1 (not_1_out, opCode[0]);
  not not_2 (not_2_out, opCode[1]);
  not not_3 (not_3_out, opCode[2]);
  not not_4 (not_4_out, opCode[3]);
  and and_1 (and_1_out, not_1_out, opCode[3], not_3_out);
  and and_2 (and_2_out, opCode[3], opCode[1], not_1_out);
  and and_3 (and_3_out, opCode[0], not_2_out, opCode[2], opCode[3]);
  or or_1 (WE, and_3_out, and_2_out, and_1_out, not_4_out);
endmodule

module ret (
  input  [3:0] opCode,
  output ret
);

  wire not_1_out, not_2_out;

  not not_1 (not_1_out, opCode[0]);
  not not_2 (not_2_out, opCode[1]);
  and and_1 (ret, not_1_out, not_2_out, opCode[2], opCode[3]);
endmodule
